# Fritzing sketch ProMicro-WT32-ETH01 (saved by Fritzing 0.9.6b)
breadboards: 1

parts:
  SparkFun_Pro_Micro1 = SparkFun Pro Micro [part_number=DEV-12640]
  A1 = wt32-eth01

nets:
  N1: SparkFun_Pro_Micro1.RAW, A1.Pin_12
  N2: SparkFun_Pro_Micro1.GND, A1.Pin_2, A1.Pin_9, A1.Pin_11, A1.Pin_14, A1.Pin_23
  N3: SparkFun_Pro_Micro1.RXI, A1.Pin_8
  N4: SparkFun_Pro_Micro1.TXO, A1.Pin_7
  N5: A1.Pin_1, A1.Pin_4
  N6: A1.Pin_3, A1.Pin_10

custom parts:
  SparkFun Pro Micro: This tiny little board does all of the neat-o Arduino tricks that you’re familiar with: 4 channels of 10-bit ADC, 5 PWM pins, 12 DIOs as well as hardware serial connections Rx and Tx. Running at 16MHz and 5V, this board will remind you a lot of your other favorite Arduino-compatible boards but this little guy can go just about anywhere. There is a voltage regulator on board so it can accept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
  wt32-eth01: WT32-ETH01 is an embedded serial port to Ethernet module based on ESP32 series designed by Wireless-Tag.
