# Fritzing sketch Nano-ESP01-BlynkNCP (saved by Fritzing 0.9.6b)
breadboards: 1

parts:
  M1 = ESP-01 Breakout Board Breadboard Adapter [part_number=ESP8266]
  Part1 = Arduino Nano (Rev3.0)
  IC1 = V_REG_LD1117VXX [package=78xxl]
  R1 = Resistor [tolerance=±5% power=0.25W resistance=220 package=THT]
  R2 = Resistor [tolerance=±5% power=0.25 resistance=220 package=THT]
  R3 = Resistor [tolerance=±5% power=0.25 resistance=220 package=THT]

nets:
  N1: M1.TXD, Part1.D10
  N2: M1.CHPD, R1.Pin_1
  N3: M1.VCC, IC1.OUT, R1.Pin_0
  N4: M1.RXD, R2.Pin_1, R3.Pin_0
  GND: M1.GND, Part1.GND, IC1.GND, R2.Pin_0
  N5: Part1.D9, R3.Pin_1
  N6: Part1.VIN, IC1.IN

notes:
  3.3v
  5v
  yellow wire goes under the Nano board
  2.2kΩ
  1kΩ
  10kΩ

custom parts:
  ESP-01 Breakout Board Breadboard Adapter: Generic WiFi Module based on the ESP8266 with onboard PCB antenna and UART communications with breadboard friendly breakout board attached.
