# Fritzing sketch PiPico-XBee-BlynkNCP (saved by Fritzing 0.9.6b)
breadboards: 1

parts:
  A1 = Raspberry Pi Pico H
  Mod1 = XBee Explorer Regulated

nets:
  N1: A1.GP0, Mod1.DIN, Mod1.DIO3
  N2: A1.GP1, Mod1.DOUT
  GND: A1.GND, Mod1.GND
  N3: A1.3V3OUT, Mod1.3.3V

custom parts:
  Raspberry Pi Pico H: Raspberry Pi Pico H. Based around the RP2040 microcontroller the Pico H is a low cost microcontroller device bringing Raspberry Pi quality, cost, and easy of use to the microcontroller space.
  XBee Explorer Regulated: Description: The XBee Explorer Regulated takes care of the 3.3V regulation, signal conditioning, and basic activity indicators (Power, RSSI and DIN/DOUT activity LEDs). It translates the 5V signals to 3.3V so that you can connect a 5V (down to 3.3V) system to any XBee module. The board was conveniently designed to mate directly with Arduino Pro boards for wireless bootloading and USB based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
