# Fritzing sketch Pro-Micro-Witty-BlynkNCP (saved by Fritzing 0.9.6b)
breadboards: 1

parts:
  SparkFun_Pro_Micro2 = SparkFun Pro Micro [part_number=DEV-12640]
  WiFi-Witty-Gizwits-ESP-12F1 = WiFi-Witty-Gizwits-ESP-12F

nets:
  N1: SparkFun_Pro_Micro2.RAW, WiFi-Witty-Gizwits-ESP-12F1.VCC
  GND: SparkFun_Pro_Micro2.GND, WiFi-Witty-Gizwits-ESP-12F1.GND
  N2: SparkFun_Pro_Micro2.RXI, WiFi-Witty-Gizwits-ESP-12F1.TXD
  N3: SparkFun_Pro_Micro2.TXO, WiFi-Witty-Gizwits-ESP-12F1.RXD

notes:
  wires go under the Witty Cloud board

custom parts:
  SparkFun Pro Micro: This tiny little board does all of the neat-o Arduino tricks that you’re familiar with: 4 channels of 10-bit ADC, 5 PWM pins, 12 DIOs as well as hardware serial connections Rx and Tx. Running at 16MHz and 5V, this board will remind you a lot of your other favorite Arduino-compatible boards but this little guy can go just about anywhere. There is a voltage regulator on board so it can accept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
  WiFi-Witty-Gizwits-ESP-12F: A breadboard friendly two part WiFi development board by Gizwits, powered by an ESP8266 ESP-12F SoC, featuring twin micro-usb ports, a photoresistor, a WS2812 RGB-LED and three buttons. The board comes in two parts. The bottom half has reset and flash buttons, a micro-usb with CH340 UART and 2x 1x08 female headers. The top half has the ESP-12F, LDR, RGB-LED, micro-usb (for power only), an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
